// Logisim project Adrika HA.circ as structural Verilog: 1 circuit, main circuit main
module main (
  input  A,
  input  B,
  output S,
  output C
);

  xor xor_1 (S, A, B);
  and and_1 (C, B, A);

  // Notes on the sheet:
  //   Half Adder
endmodule
