// Logisim project Binary_4_bit_incrementer_circuit.circ as structural Verilog: 1 circuit, main circuit main
module main (
  input  A3,
  input  A2,
  input  A1,
  input  A0,
  output Cout,
  output S3,
  output S2,
  output S1,
  output S0
);

  wire main_1_p4, main_2_p4, main_3_p4;

  // half_adder_for_binary4bit_incremt_circuit_main main_1: pin names not known; wires that end beside it: Cout, A3, S3, main_1_p4
  // half_adder_for_binary4bit_incremt_circuit_main main_2: pin names not known; wires that end beside it: main_1_p4, A2, S2, main_2_p4
  // half_adder_for_binary4bit_incremt_circuit_main main_3: pin names not known; wires that end beside it: main_2_p4, A1, S1, main_3_p4
  // half_adder_for_binary4bit_incremt_circuit_main main_4: pin names not known; wires that end beside it: main_3_p4, A0, S0, 1'b1

  // Notes on the sheet:
  //   C2
  //   Binary 4 Bit Incrementer Circuit
  //   C1
  //   C0
  //   1
endmodule
