// Logisim project full_adder.circ as structural Verilog: 1 circuit, main circuit main
module main (
  input  A,
  input  B,
  input  Cin,
  output S,
  output Cout
);

  wire main_1_c, main_1_s, main_2_c;

  Adrika_HA_main main_1 (.A(A), .B(B), .S(main_1_s), .C(main_1_c));
  Adrika_HA_main main_2 (.A(main_1_s), .B(Cin), .S(S), .C(main_2_c));
  or or_1 (Cout, main_2_c, main_1_c);

  // Notes on the sheet:
  //   A XOR B
  //   A AND B
  //   Full Adder Using Half Adder
  //   (A XOR B) AND Cin
  //   A XOR B XOR Cin
endmodule
