// Logisim project halfr_subtractor.circ as structural Verilog: 1 circuit, main circuit main
module main (
  input  A,
  input  B,
  output D,
  output Br
);

  wire not_1_out;

  not not_1 (not_1_out, A);
  xor xor_1 (D, A, B);
  and and_1 (Br, B, not_1_out);

  // Notes on the sheet:
  //   Half Subtractor
  //   A XOR B
  //   A' AND B
endmodule
